// Digital circuit CPU.dig as structural Verilog
module CPU (
  input  clk
);

  wire comparator_1_eq, comparator_2_eq;
  wire [7:0] rom_1_d, rom_2_d;
  wire [15:0] rom_3_d, undriven;

  ROM #(.AddrBits(16), .Bits(8)) rom_1 (.A(undriven), .sel(1'b1), .D(rom_1_d));
  ROM #(.AddrBits(16), .Bits(8)) rom_2 (.A(undriven), .sel(1'b1), .D(rom_2_d));
  ROM #(.AddrBits(16), .Bits(16)) rom_3 (.A(undriven), .sel(1'b1), .D(rom_3_d));
  // ALU alu_1: pin names not known; wires that end beside it: rom_1_d, rom_2_d, clk, rom_2_d
  Comparator #(.Bits(8)) comparator_1 (.a(rom_1_d), .b(8'h1), .eq(comparator_1_eq));  // open: gt, lt
  Comparator #(.Bits(8)) comparator_2 (.a(rom_1_d), .b(8'h1), .eq(comparator_2_eq));  // open: gt, lt
  RAMDualPort #(.AddrBits(16), .Bits(8)) ramdualport_1 (
    .A(rom_3_d), .Din(rom_2_d), .str(comparator_1_eq), .C(clk), .ld(comparator_2_eq), .D(rom_2_d));

  // Notes on the sheet:
  //   clk: Hz: 10
  //   LN: output from the programmme counter,
  //   the current line of code being executed
  //   LN
  //   CMD
  //   DAT
  //   ADR
  //   CLK
endmodule
